# Fritzing sketch RoboChess_Skem (saved by Fritzing 0.8.7b)
breadboards: 1

parts:
  Εξάρτημα1 = Arduino Board Ethernet
  Εξάρτημα2 = FTDI Basic Programmer

nets:
  GND: Εξάρτημα1.GND, Εξάρτημα2.GND
  N1: Εξάρτημα1.5V, Εξάρτημα2.POWER
  N2: Εξάρτημα1.PD0, Εξάρτημα2.TXO
  N3: Εξάρτημα1.PD1, Εξάρτημα2.RXI
  N4: Εξάρτημα1.RTS, Εξάρτημα2.DTR

notes:
  TTL 1 INPUT
  TTL 2 INPUT
  TTL 3 INPUT
  TTL 4 INPUT
  TTL5 INPUT
  TTL 6 INPUT
  TTL 7 INPUT
  TTL 1 OUTPUT
  Serial Communication with Python
